# Fritzing sketch CircuitDiagram (saved by Fritzing 0.9.3b)
breadboards: 1

parts:
  LED3 = smd LED [color="Green (570nm)" package="1206 [SMD]"]
  LED3_2 = smd LED [color="Green (570nm)" package="1206 [SMD]"]
  R3 = Resistor [tolerance=±5% resistance=220 package="2512 [SMD]"]
  R14 = PHOTOCELL [package=photocell]
  R15 = Resistor [tolerance=±5% resistance=10k package="2512 [SMD]"]
  J1 = Infrared Proximity Sensor
  U1 = ESP32S-HiLetgo [part_number=ESP32S-HiLetgo]

nets:
  N1: LED3.cathode, LED3_2.cathode, R3.Pin_0
  N2: LED3.anode, LED3_2.anode, U1.GPIO36
  N3: R3.Pin_1, R15.Pin_1, J1.GND, U1.3.3
  N4: R14.P$1, R15.Pin_0, U1.GPIO1
  N5: R14.P$2, J1.Vcc, U1.GPIO23

custom parts:
  ESP32S-HiLetgo: HiLetgo ESP-WROOM-32 ESP32 ESP-32S Development Board 2.4GHz Dual-Mode WiFi + Bluetooth Dual Cores Microcontroller The ESP32 integrated with Antenna switches, RF Balun, power amplifiers, low-noise amplifiers, filters, and management modules, and the entire solution occupies the least area of PCB. 2.4 GHz Wi-Fi plus Bluetooth dual-mode chip, with TSMC Ultra-low power consumption 40nm technology,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
